// Logisim project cpu.circ as structural Verilog: 1 circuit, main circuit cpu
module cpu (
  input  clk,
  input  [31:0] Instruction,
  input  [31:0] MemReadData,
  output [31:0] MemAddress,
  output [31:0] ProgramCounter,
  output [31:0] ra,
  output [31:0] sp,
  output [31:0] t0,
  output [31:0] t1,
  output [31:0] t2,
  output [31:0] s0,
  output [31:0] s1,
  output [31:0] a0,
  output [3:0] MemWriteMask,
  output [31:0] MemWriteData,
  output [4:0] RIDX2,
  output [4:0] WriteIndex,
  output [31:0] WriteData,
  output [31:0] PCInput,
  output [4:0] RIDX1,
  output [4:0] I_rd,
  output ASel,
  output BrEq,
  output BSel,
  output BrLt,
  output [4:0] I_rs1,
  output [3:0] out_27,
  output PCSel,
  output [31:0] ALU_RES,
  output [31:0] Imm,
  output [31:0] ALU_A,
  output [31:0] ALU_B,
  output [31:0] RD1,
  output [31:0] RD2
);

  wire branch_comp_1_p4, BrUn, MemWEn, RegWEn;
  wire [1:0] WBSel;
  wire [2:0] ImmSel;
  wire [31:0] LoadedData, PC_PLUS_4;

  Adder #(.width(32)) adder_1 (.a(ProgramCounter), .b(32'h4), .out(PC_PLUS_4));  // open: cin, cout
  Register #(.width(32)) PC (.D(PCInput), .clk(clk), .Q(ProgramCounter));  // open: en, clr
  Multiplexer #(.width(32)) multiplexer_1 (.in0(PC_PLUS_4), .in1(ALU_RES), .out(PCInput), .sel(PCSel));
  control_logic control_logic_1 (
    .Instruction(Instruction), .BrEq(BrEq), .BrLt(BrLt), .PCSel(PCSel), .RegWEn(RegWEn), .ImmSel(ImmSel),
    .BrUn(BrUn), .ASel(ASel), .BSel(BSel), .ALUSel(out_27), .MemWEn(MemWEn), .WBSel(WBSel));
  regfile regfile_1 (
    .ReadIndex1(Instruction[19:15]), .ReadIndex2(Instruction[24:20]), .WriteIndex(Instruction[11:7]),
    .WriteData(WriteData), .RegWEn(RegWEn), .clk(clk), .ra(ra), .sp(sp), .t0(t0), .t1(t1), .t2(t2), .s0(s0),
    .s1(s1), .a0(a0), .ReadData1(RD1), .ReadData2(RD2));
  Multiplexer #(.width(32)) multiplexer_2 (.in0(RD1), .in1(ProgramCounter), .out(ALU_A), .sel(ASel));
  Multiplexer #(.width(32)) multiplexer_3 (.in0(RD2), .in1(Imm), .out(ALU_B), .sel(BSel));
  imm_gen imm_gen_1 (.Instruction(Instruction), .ImmSel(ImmSel), .Immediate(Imm));
  alu alu_1 (.A(ALU_A), .B(ALU_B), .ALUSel(out_27), .ALUResult(ALU_RES));
  // branch_comp branch_comp_1: pin names not known; wires that end beside it: BrUn, RD1, RD2, branch_comp_1_p4, BrEq, BrLt
  partial_store partial_store_1 (
    .Instruction(Instruction), .MemAddress(ALU_RES), .DataFromReg(RD2), .MemWEn(MemWEn),
    .MemWriteMask(MemWriteMask), .DataToMem(MemWriteData));
  partial_load partial_load_1 (
    .Instruction(Instruction), .MemAddress(ALU_RES), .DataFromMem(MemReadData), .DataToReg(LoadedData));
  Multiplexer #(.select(2), .width(32)) multiplexer_4 (
    .in0(LoadedData), .in1(ALU_RES), .in2(PC_PLUS_4), .out(WriteData), .sel(WBSel));  // open: in3

  assign I_rd = Instruction[11:7];
  assign I_rs1 = Instruction[19:15];
  assign MemAddress = ALU_RES;
  assign RIDX1 = Instruction[19:15];
  assign RIDX2 = Instruction[24:20];
  assign WriteIndex = Instruction[11:7];

  // Other names for the same wires on the sheet: ALUSel[3:0] = out_27; Immediate[31:0] = Imm;
  //   Opcode[6:0] = Instruction[6:0]; Instruction31_7[24:0] = Instruction[31:7]; rd[4:0] = Instruction[11:7];
  //   I_funct3[2:0] = Instruction[14:12]; ReadIndex1[4:0] = Instruction[19:15]; rs1[4:0] = Instruction[19:15];
  //   ReadIndex2[4:0] = Instruction[24:20]; rs2[4:0] = Instruction[24:20]; funct7[6:0] = Instruction[31:25];
  //   ProgramCounterInput[31:0] = PCInput; ReadData1[31:0] = RD1; ReadData2[31:0] = RD2

  // Notes on the sheet:
  //   To IMEM
  //   IMEM (do **NOT** move this)
  //   From IMEM
  //   Inputs/Outputs for testing. Do **NOT** move these.
  //   It is OK to move the PC, RegFile, ALU, MEM, Branch Comp, Imm Gen, Partial Load, Partial Store and Control Logic to wherever is most convenient for you when constructing your CPU, and to delete this text
  //   To DMEM
  //   DMEM (do **NOT** move this)
  //   From DMEM
endmodule
